# Fritzing sketch ar03 01 (saved by Fritzing 0.9.3b)
breadboards: 1

parts:
  부품1 = Arduino Uno (Rev3)
  LED1 = LED - 5mm [color="Red (633nm)" package="5 mm [THT]"]
  LED2 = LED - 5mm [color="Red (633nm)" package="5 mm [THT]"]
  R1 = Resistor [tolerance=±5% resistance=220 package=THT]
  R2 = Resistor [tolerance=±5% resistance=220 package=THT]  # not connected

nets:
  N1: 부품1.D3_PWM, LED1.cathode
  N2: 부품1.D5_PWM, 부품1.5V, LED2.anode
  N3: R1.Pin_0, R1.Pin_1
